# Fritzing sketch Blutooth pairing (saved by Fritzing 0.9.3b)
breadboards: 1

parts:
  Part1 = Arduino Uno (Rev3)
  Part2 = Bluetooth HC-05 Macho
  R1 = Resistor [tolerance=±5% resistance=1k package=THT]
  R3 = Resistor [tolerance=±5% resistance=2.2k package=THT]

nets:
  N1: Part1.D0/RX, R1.Pin_0
  N2: Part1.D1/TX, Part2.TXD
  5V: Part1.5V, Part2.VCC
  GND: Part1.GND, Part2.GND, R3.Pin_0
  N3: Part2.RXD, R1.Pin_1, R3.Pin_1
